# Fritzing sketch CABLAGE TELESIEGE (saved by Fritzing 0.9.3b)
breadboards: 1

parts:
  S1 = Pushbutton [package="[THT]"]
  BAT1 = BC9VPC [package=bc9vpc]
  Q1 = pnp-Powertransistor [package="TO220 [THT]"]
  Composant1 = Arduino Uno (Rev3) - ICSP
  R1 = Resistor [tolerance=±5% resistance=10k package="2010 [SMD]"]
  D1 = Rectifier Diode [part_number=1N4001 package="300 mil [THT]"]
  M1 = DC Motor
  R3 = Resistor [tolerance=±5% resistance=2.2k package="0603 [SMD]"]
  R4 = Resistor [tolerance=±5% resistance=10k package="2512 [SMD]"]
  S2 = Pushbutton [package="[SMD]"]

nets:
  N1: S1.Pin_1, S1.Pin_2, Composant1.D2, R1.Pin_1
  N2: S1.Pin_3, S1.Pin_4
  N3: BAT1.V+, D1.cathode, M1.pin_2
  N4: BAT1.V-, Q1.emitter, R1.Pin_0, R4.Pin_0, S2.Pin_3, S2.Pin_4
  N5: Q1.base, R3.Pin_1
  N6: Q1.collector, D1.anode, M1.pin_1
  N7: Composant1.D9_PWM, R3.Pin_0
  N8: Composant1.D5_PWM, R4.Pin_1, S2.Pin_1, S2.Pin_2
